// Logisim project subleq.circ as structural Verilog: 5 circuits, main circuit main
module main (
  input  RST
);

  wire clk, d_ff_1_qn, dpram2_1_ckout, dpram2_1_clr, dpram2_1_ld, dpram2_1_sel, dpram2_1_str, execute, fetch,
       leqzero, memclk;
  wire [7:0] dataC, dpram2_1_a, dpram2_1_d, dpram2_1_data_a, dpram2_1_data_b, multiplexer_1_out, PC,
       pc_increment_1_pcout, ram_1_data;
  wire [23:0] instr_out, rom_1_data;

  Clock clock_1 (.out(memclk));
  D_Flip_Flop d_ff_1 (.clk(memclk), .D(d_ff_1_qn), .Q(clk), .Qn(d_ff_1_qn));  // open: preset, en, reset
  ROM #(.dataWidth(24)) rom_1 (.addr(PC), .data(rom_1_data), .sel(1'b1));
  Register #(.width(24)) IR (.D(rom_1_data), .en(fetch), .Q(instr_out), .clk(clk), .clr(RST));
  Sequencer sequencer_1 (.RST(RST), .Clk(clk), .F(fetch), .E(execute));
  // Probe on instr_out
  // Probe on fetch
  // Probe on execute
  pc_increment pc_increment_1 (.clk(clk), .fetch(fetch), .pc(PC), .PCout(pc_increment_1_pcout));
  Multiplexer #(.width(8)) multiplexer_1 (
    .in0(pc_increment_1_pcout), .in1(instr_out[7:0]), .out(multiplexer_1_out), .sel(leqzero));
  RAM #(.bus("separate")) ram_1 (
    .addr(dpram2_1_a), .din(dpram2_1_d), .data(ram_1_data), .str(dpram2_1_str), .sel(dpram2_1_sel),
    .clk(dpram2_1_ckout), .ld(dpram2_1_ld), .clr(dpram2_1_clr));
  // Probe on PC
  Register u_PC (.D(multiplexer_1_out), .en(execute), .Q(PC), .clk(clk), .clr(RST));
  // Probe on dpram2_1_data_a
  dpram2 dpram2_1 (
    .WE(execute), .Addr_A(instr_out[23:16]), .Addr_B(instr_out[15:8]), .Addr_C(instr_out[15:8]),
    .dataC(dataC), .memclk(memclk), .Data_A(dpram2_1_data_a), .Data_B(dpram2_1_data_b), .A(dpram2_1_a),
    .D(dpram2_1_d), .str(dpram2_1_str), .ckOut(dpram2_1_ckout), .ld(dpram2_1_ld), .clr(dpram2_1_clr),
    .oD(ram_1_data), .sel(dpram2_1_sel));
  // Probe on dpram2_1_data_b
  ALU alu_1 (.A(dpram2_1_data_a), .B(dpram2_1_data_b), .O(dataC), .LEQZERO(leqzero));  // open: CO
  // Probe on dataC
  // Probe on leqzero

  // Notes on the sheet:
  //   Rom
  //   contents of rom_1 (hex, n*v repeats v):
  //   10203 123405 51720 101010 10101 10201 50103 20301 101010 320010 201010 323201 4*0 122321 456110
  //   abcdef
  //   PC Increment
endmodule

module ALU (
  input  [7:0] A,
  input  [7:0] B,
  output [7:0] O,
  output LEQZERO,
  output CO
);

  wire bitselector_1_out, comparator_1_eq;
  wire [7:0] not_1_out;

  assign not_1_out = ~B;  // NOT_Gate not_1, 8 bits wide
  Adder adder_1 (.a(A), .b(not_1_out), .out(O), .cin(1'b1), .cout(CO));
  Comparator comparator_1 (.a(O), .b({8{1'b0}}), .eq(comparator_1_eq));  // open: gt, lt
  BitSelector bitselector_1 (.in(O), .out(bitselector_1_out), .sel(3'b111));
  or or_1 (LEQZERO, comparator_1_eq, bitselector_1_out);

  // Notes on the sheet:
  //   ALU
endmodule

module Sequencer (
  input  RST,
  input  Clk,
  output F,
  output E
);

  wire and_1_out, q1;

  and and_1 (and_1_out, ~RST, ~q1);  // AND_Gate
  D_Flip_Flop d_ff_1 (.clk(Clk), .D(and_1_out), .Q(q1), .en(1'b1), .reset(RST));  // open: Qn, preset
  not not_1 (F, q1);
  buf buffer_1 (E, q1);
endmodule

module pc_increment (
  input  clk,
  input  fetch,
  input  [7:0] pc,
  output [7:0] PCout
);

  wire [7:0] adder_1_out;

  Adder adder_1 (.a(pc), .b(8'h1), .out(adder_1_out));  // open: cin, cout
  Register register_1 (.D(adder_1_out), .en(fetch), .Q(PCout), .clk(clk));  // open: clr
endmodule

module dpram2 (
  input  [7:0] oD,
  input  WE,
  input  [7:0] Addr_A,
  input  [7:0] Addr_B,
  input  [7:0] Addr_C,
  input  [7:0] dataC,
  input  memclk,
  output [7:0] A,
  output [7:0] D,
  output [7:0] Data_A,
  output str,
  output sel,
  output ckOut,
  output ld,
  output clr,
  output [7:0] Data_B
);

  wire not_1_out, not_2_out;

  Multiplexer #(.select(2), .width(8)) multiplexer_1 (
    .in0(Addr_A), .in1(Addr_B), .in2(Addr_C), .in3(Addr_C), .out(A), .sel({WE, memclk}));
  not not_1 (not_1_out, WE);
  not not_2 (not_2_out, memclk);
  Register register_1 (.D(oD), .en(not_1_out), .Q(Data_A), .clk(memclk), .clr(1'b0));
  Register register_2 (.D(oD), .en(not_1_out), .Q(Data_B), .clk(not_2_out), .clr(1'b0));

  assign ckOut = memclk;
  assign clr = 1'b0;
  assign D = dataC;
  assign ld = 1'b1;
  assign sel = 1'b1;
  assign str = WE;

  // Notes on the sheet:
  //   Address A/B -> memclk
  //   Address AB/C -> WE
  //   enable A reg ->memclk
  //   enable B reg->!memclk
endmodule
